// Logisim project HW1.circ as structural Verilog: 1 circuit, main circuit main
module main (
  input  A1,
  input  B1,
  input  A0,
  input  B0
);

  wire nand_1_out, nand_2_out, nand_3_out, nor_1_out, nor_2_out, nor_3_out, nor_4_out, nor_5_out, nor_6_out,
       nor_7_out, nor_8_out, not_1_out, not_2_out, not_3_out, not_4_out, not_5_out, not_6_out, not_7_out,
       not_8_out, not_9_out, not_10_out, not_11_out, not_12_out;

  not not_1 (not_1_out, B1);
  not not_2 (not_2_out, B0);
  nand nand_1 (nand_1_out, A1, not_1_out);
  nor nor_1 (nor_1_out, A1, B1);
  nor nor_2 (nor_2_out, A0, B0);
  nand nand_2 (nand_2_out, A0, not_2_out);
  not not_3 (not_3_out, nand_1_out);
  not not_4 (not_4_out, A1);
  nor nor_3 (nor_3_out, not_4_out, not_5_out);
  not not_5 (not_5_out, B1);
  not not_6 (not_6_out, A0);
  nor nor_4 (nor_4_out, not_6_out, not_7_out);
  not not_7 (not_7_out, B0);
  not not_8 (not_8_out, nand_2_out);
  nor nor_5 (nor_5_out, nor_1_out, nor_3_out);
  nor nor_6 (nor_6_out, nor_2_out, nor_4_out);
  not not_9 (not_9_out, nor_5_out);
  // Probe on nor_7_out
  nor nor_7 (nor_7_out, nor_5_out, nor_6_out);
  not not_10 (not_10_out, nand_3_out);
  nand nand_3 (nand_3_out, not_9_out, not_8_out);
  nor nor_8 (nor_8_out, not_3_out, not_10_out);
  not not_11 (not_11_out, nor_8_out);
  not not_12 (not_12_out, not_11_out);
  // Probe on not_11_out
  // Probe on not_12_out

  // Notes on the sheet:
  //    Компаратор двух 2-битных входов с выходами LEQ, EQ, G.
  //   Ермолин Кирилл, Б01-407
  //   EQ
  //   G
  //   LEQ
endmodule
